# Fritzing sketch Schematic Fritzing (saved by Fritzing 0.9.3b)
breadboards: 1

parts:
  M1 = MAX485 Breakout [package=THT]
  Part1 = Arduino Uno (Rev3) - ICSP
  A1 = JXBS-3001-NPK-RS
  BAT1 = BC9VPC [package=bc9vpc]
  M2 = DOIT Esp32 DevKit v1 (30 pins long, 11 pins width) [part_number=ESP32S-PIN30]

nets:
  N1: M1.RO, Part1.D2
  N2: M1.RE, Part1.D13/SCK
  N3: M1.DE, Part1.D12/MISO
  N4: M1.DI, Part1.D3_PWM
  GND: M1.GND, Part1.GND, M2.GND
  N5: M1.A, A1.Pin_4
  N6: M1.B, A1.Pin_3
  VCC: M1.VCC, Part1.5V
  N7: Part1.D0/RX, M2.TX2
  N8: Part1.D1/TX, M2.RX2
  VIN: Part1.VIN, M2.VIN
  N9: A1.Pin_1, BAT1.V+
  N10: A1.Pin_2, BAT1.V-

custom parts:
  MAX485 Breakout: MAX485 RS485 breakout board
  JXBS-3001-NPK-RS: The NPK sensor is designed for detecting the content of nitrogen, phosphorus and potassium in soil, determining the fertility of the soil and facilitating the evaluation of the soil condition by the customer system.
  DOIT Esp32 DevKit v1 (30 pins long, 11 pins width): The DOIT Esp32 DevKit v1 is one of the development board created by DOIT to evaluate the ESP-WROOM-32 module. It is based on the ESP32 microcontroller that boasts Wifi, Bluetooth, Ethernet and Low Power support all in a single chip. (vanepp) made breadboard work, adjusted pin numbering and labels and reduced size of schematic and cleaned up pcb. This chip is 30pins long (2 x15) and 11 pins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
