# Fritzing sketch salak-skematik (saved by Fritzing 0.9.3b)

parts:
  M9 = MAX485 Breakout [package=THT]
  M10 = MT3608 Module
  S4 = Round Pushbutton  # not connected
  M11 = DOIT Esp32 DevKit v1 (30 pins long, 11 pins width) [part_number=ESP32S-PIN30]
  LCD2004-I2C1 = LCD2004-I2C
  VCC7 = Battery
  S5 = SPST Switch [package=r_sw_th]  # not connected
  A3 = JXBS-3001-NPK-RS smaller
  U2 = LM2596 step down module
  S6 = SPST Switch [package=r_sw_th]  # not connected
  VCC9 = Battery
  VCC10 = Battery
  LCD2004-I2C2 = LCD2004-I2C
  A4 = JXBS-3001-NPK-RS smaller
  M12 = MAX485 Breakout [package=THT]
  M13 = MT3608 Module
  S7 = Round Pushbutton  # not connected
  M14 = DOIT Esp32 DevKit v1 (30 pins long, 11 pins width) [part_number=ESP32S-PIN30]

nets:
  N1: M9.RO, M11.RX0
  N2: M9.RE, M9.DE, M11.D2
  N3: M9.DI, M11.TX0
  GND: M9.GND, M10.pin1, M11.GND, LCD2004-I2C1.GND, VCC7.-
  N4: M9.A, A3.Pin_3
  N5: M9.B, A3.Pin_4
  VCC: M9.VCC, M10.pin2, M11.VIN, LCD2004-I2C1.VCC, VCC7.+
  N6: M10.pin3, A3.Pin_1
  N7: M10.pin4, A3.Pin_2
  N8: M11.D21, LCD2004-I2C1.SDA
  N9: M11.D22, LCD2004-I2C1.SCL
  N10: U2.IN+, VCC9.+
  GND_2: U2.IN-, U2.OUT-, VCC9.-, LCD2004-I2C2.GND, M12.GND, M14.GND
  VCC_2: U2.OUT+, LCD2004-I2C2.VCC, M12.VCC, M14.VIN
  N11: VCC10.-, M13.pin1
  N12: VCC10.+, M13.pin2
  N13: LCD2004-I2C2.SDA, M14.D21
  N14: LCD2004-I2C2.SCL, M14.D22
  N15: A4.Pin_1, M13.pin3
  N16: A4.Pin_2, M13.pin4
  N17: A4.Pin_3, M12.A
  N18: A4.Pin_4, M12.B
  N19: M12.RO, M14.RX0, M14.D34
  N20: M12.RE, M12.DE, M14.D2
  N21: M12.DI, M14.TX0

custom parts:
  MAX485 Breakout: MAX485 RS485 breakout board
  MT3608 Module: MT3608 Boost Converter Module Links: Aerosemi MT3608 2A Step Up Converter datasheet
  DOIT Esp32 DevKit v1 (30 pins long, 11 pins width): The DOIT Esp32 DevKit v1 is one of the development board created by DOIT to evaluate the ESP-WROOM-32 module. It is based on the ESP32 microcontroller that boasts Wifi, Bluetooth, Ethernet and Low Power support all in a single chip. (vanepp) made breadboard work, adjusted pin numbering and labels and reduced size of schematic and cleaned up pcb. This chip is 30pins long (2 x15) and 11 pins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
  LCD2004-I2C: A standard character display with 4x20 characters. Comes in many colors with LCM2004 IIC attached.
  Battery: Your standard 2x 18650 battery pack (7,4 Volts)
  JXBS-3001-NPK-RS smaller: The NPK sensor is designed for detecting the content of nitrogen, phosphorus and potassium in soil, determining the fertility of the soil and facilitating the evaluation of the soil condition by the customer system. This version has breadboard reduced in size to more closely match the 485 adapter and CPU board.
  LM2596 step down module: LM2596 DC-DC step down power supply module 3 A.
