# Fritzing sketch salak-skematikV20 (saved by Fritzing 1.0.2b)

parts:
  U3 = LM2596 step down module
  S8 = SPST Switch [package=r_sw_th]  # not connected
  VCC11 = Battery
  VCC12 = Battery
  LCD2004-I2C3 = LCD2004-I2C
  A5 = JXBS-3001-NPK-RS smaller
  M15 = MAX485 Breakout [package=THT]
  M16 = MT3608 Module
  S9 = Round Pushbutton  # not connected
  M17 = DOIT Esp32 DevKit v1 (30 pins long, 11 pins width) [part_number=ESP32S-PIN30]

nets:
  N1: U3.IN+, VCC11.+
  GND: U3.IN-, U3.OUT-, VCC11.-, LCD2004-I2C3.GND, M15.GND, M17.GND
  VCC: U3.OUT+, LCD2004-I2C3.VCC, M15.VCC, M17.VIN
  N2: VCC12.-, M16.pin1
  N3: VCC12.+, M16.pin2
  N4: LCD2004-I2C3.SDA, M17.D21
  N5: LCD2004-I2C3.SCL, M17.D22
  N6: A5.Pin_1, M16.pin3
  N7: A5.Pin_2, M16.pin4
  N8: A5.Pin_3, M15.A
  N9: A5.Pin_4, M15.B
  N10: M15.RO, M17.RX0, M17.D34
  N11: M15.RE, M15.DE, M17.D2
  N12: M15.DI, M17.TX0

custom parts:
  LM2596 step down module: LM2596 DC-DC step down power supply module 3 A.
  Battery: Your standard 2x 18650 battery pack (7,4 Volts)
  LCD2004-I2C: A standard character display with 4x20 characters. Comes in many colors with LCM2004 IIC attached.
  JXBS-3001-NPK-RS smaller: The NPK sensor is designed for detecting the content of nitrogen, phosphorus and potassium in soil, determining the fertility of the soil and facilitating the evaluation of the soil condition by the customer system. This version has breadboard reduced in size to more closely match the 485 adapter and CPU board.
  MAX485 Breakout: MAX485 RS485 breakout board
  MT3608 Module: MT3608 Boost Converter Module Links: Aerosemi MT3608 2A Step Up Converter datasheet
  DOIT Esp32 DevKit v1 (30 pins long, 11 pins width): The DOIT Esp32 DevKit v1 is one of the development board created by DOIT to evaluate the ESP-WROOM-32 module. It is based on the ESP32 microcontroller that boasts Wifi, Bluetooth, Ethernet and Low Power support all in a single chip. (vanepp) made breadboard work, adjusted pin numbering and labels and reduced size of schematic and cleaned up pcb. This chip is 30pins long (2 x15) and 11 pins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
