# Fritzing sketch salak-skematikV21 (saved by Fritzing 1.0.2b)

parts:
  M9 = MAX485 Breakout [package=THT]
  M10 = MT3608 Module
  S4 = Round Pushbutton
  M11 = DOIT Esp32 DevKit v1 (30 pins long, 11 pins width) [part_number=ESP32S-PIN30]
  LCD2004-I2C1 = LCD2004-I2C
  VCC7 = Battery
  A3 = JXBS-3001-NPK-RS smaller

nets:
  N1: M9.RO, M11.RX0
  N2: M9.RE, M9.DE, M11.D2
  N3: M9.DI, M11.TX0
  GND: M9.GND, S4.leg0, M11.GND, LCD2004-I2C1.GND
  N4: M9.A, A3.Pin_3
  N5: M9.B, A3.Pin_4
  VCC: M9.VCC, M10.pin2, M11.VIN, LCD2004-I2C1.VCC, VCC7.+
  N6: M10.pin1, S4.leg1, VCC7.-
  N7: M10.pin3, A3.Pin_1
  N8: M10.pin4, A3.Pin_2
  N9: M11.D21, LCD2004-I2C1.SDA
  N10: M11.D22, LCD2004-I2C1.SCL

custom parts:
  MAX485 Breakout: MAX485 RS485 breakout board
  MT3608 Module: MT3608 Boost Converter Module Links: Aerosemi MT3608 2A Step Up Converter datasheet
  DOIT Esp32 DevKit v1 (30 pins long, 11 pins width): The DOIT Esp32 DevKit v1 is one of the development board created by DOIT to evaluate the ESP-WROOM-32 module. It is based on the ESP32 microcontroller that boasts Wifi, Bluetooth, Ethernet and Low Power support all in a single chip. (vanepp) made breadboard work, adjusted pin numbering and labels and reduced size of schematic and cleaned up pcb. This chip is 30pins long (2 x15) and 11 pins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
  LCD2004-I2C: A standard character display with 4x20 characters. Comes in many colors with LCM2004 IIC attached.
  Battery: Your standard 2x 18650 battery pack (7,4 Volts)
  JXBS-3001-NPK-RS smaller: The NPK sensor is designed for detecting the content of nitrogen, phosphorus and potassium in soil, determining the fertility of the soil and facilitating the evaluation of the soil condition by the customer system. This version has breadboard reduced in size to more closely match the 485 adapter and CPU board.
